// Logisim project Brainfunk.circ as structural Verilog: 1 circuit, main circuit Brainfunk_CPU
module Brainfunk_CPU (
);

  wire and_1_out, and_2_out, CLK, CLK_STOP, clock_1_out, comparator_1_eq, DATA_BYPASS, HALT_OP, IO_OP, IO_RD,
       IO_WAIT, IO_WR, JE_INST, JN_INST, keyboard_1_avail, MAR_WR, MEM_WR, nand_2_out, not_1_out, not_2_out,
       or_1_out, RST;
  wire [3:0] INST_OP;
  wire [6:0] keyboard_1_data;
  wire [6:6] rom_1_data;
  wire [7:0] adder_3_out, bit_extender_2_out, INST_DATA8, MEM_RD_BUS, multiplexer_2_out, multiplexer_3_out;
  wire [11:0] INST_OFFSET12;
  wire [15:0] adder_1_out, bit_extender_1_out, MEM_ADDR;
  wire [19:0] adder_2_out, CODE_ADDR, multiplexer_1_out;

  Button button_1 (.out(RST));
  not not_1 (not_1_out, comparator_1_eq);
  Comparator #(.mode("unsigned")) comparator_1 (.a(MEM_RD_BUS), .b({8{1'b0}}), .eq(comparator_1_eq));  // open: gt, lt
  Bit_Extender #(.in_width(20)) bit_extender_1 (.in({INST_OFFSET12, INST_DATA8}), .out(bit_extender_1_out));
  ROM #(.addrWidth(4)) rom_1 (
    .addr(INST_OP), .data({DATA_BYPASS, rom_1_data[6], HALT_OP, IO_OP, JE_INST, JN_INST, MAR_WR, MEM_WR}));
  Clock clock_1 (.out(clock_1_out));
  nand nand_1 (CLK, clock_1_out, CLK_STOP);
  and and_1 (and_1_out, JN_INST, not_1_out);
  and and_2 (and_2_out, JE_INST, comparator_1_eq);
  Register #(.width(16)) MAR (.D(adder_1_out), .en(MAR_WR), .clk(CLK), .Q(MEM_ADDR), .clr(RST));
  Adder #(.width(16)) adder_1 (.a(MEM_ADDR), .b(bit_extender_1_out), .out(adder_1_out), .cin(1'b0));  // open: cout
  Multiplexer #(.width(20)) multiplexer_1 (
    .in0(20'h1), .in1({INST_OFFSET12, INST_DATA8}), .out(multiplexer_1_out), .sel(or_1_out));
  or or_1 (or_1_out, and_1_out, and_2_out);
  not not_2 (not_2_out, INST_DATA8[0]);
  Adder #(.width(20)) adder_2 (.a(CODE_ADDR), .b(multiplexer_1_out), .out(adder_2_out), .cin(1'b0));  // open: cout
  and and_3 (IO_RD, not_2_out, IO_OP);
  and and_4 (IO_WR, IO_OP, INST_DATA8[0]);
  Register #(.width(20)) PC (.D(adder_2_out), .en(nand_2_out), .clk(CLK), .Q(CODE_ADDR), .clr(RST));
  nand nand_2 (nand_2_out, IO_WAIT, IO_RD);
  // Probe on CODE_ADDR
  ROM #(.addrWidth(20), .dataWidth(24)) CODE_ROM (.addr(CODE_ADDR), .data({INST_OP, INST_OFFSET12, INST_DATA8}));
  Keyboard keyboard_1 (.clk(CLK), .re(IO_RD), .avail(keyboard_1_avail), .data(keyboard_1_data));  // open: clr
  Adder adder_3 (.a(MEM_RD_BUS), .b(INST_DATA8), .out(adder_3_out), .cin(1'b0));  // open: cout
  D_Flip_Flop d_ff_1 (.D(HALT_OP), .clk(CLK), .Qn(CLK_STOP), .reset(RST));  // open: Q, preset
  Multiplexer #(.width(8)) multiplexer_2 (
    .in0(adder_3_out), .in1(INST_DATA8), .out(multiplexer_2_out), .sel(DATA_BYPASS));
  not not_3 (IO_WAIT, keyboard_1_avail);
  // Probe on {INST_OP, INST_OFFSET12, INST_DATA8}
  Multiplexer #(.width(8)) multiplexer_3 (
    .in0(multiplexer_2_out), .in1(bit_extender_2_out), .out(multiplexer_3_out), .sel(IO_RD));
  assign bit_extender_2_out = {{1{1'b0}}, keyboard_1_data};  // Bit_Extender bit_extender_2
  // Probe on {INST_OFFSET12, INST_DATA8}
  // Probe on INST_OP
  RAM #(.addrWidth(16), .clearpin("true"), .enables("line")) DATA_RAM (
    .addr(MEM_ADDR), .we(MEM_WR), .clk(CLK), .din(multiplexer_3_out), .dout(MEM_RD_BUS), .clr(RST));
  // Probe on INST_OFFSET12
  TTY #(.cols(80), .rows(25)) tty_1 (.data(MEM_RD_BUS[6:0]), .clk(CLK), .we(IO_WR), .clr(RST));
  // Probe on INST_DATA8

  // Other names for the same wires on the sheet: INST_OFFSET20[19:0] = {INST_OFFSET12, INST_DATA8}

  // Notes on the sheet:
  //   contents of rom_1 (hex, n*v repeats v):
  //   20 1 81 20 20 2 8 4 10 20
  //   contents of CODE_ROM (hex, n*v repeats v):
  //   100010 600006 500001 100005 5fffff 1000ff 7ffffc 500001 600006 5fffff 100005 500001 1000ff 7ffffc
  //   100001 5fffff 100001 600061 500001 600008 500001 100001 500001 100001 5ffffe 1000ff 7ffffa 100002
  //   500002 600006 5ffffe 100001 500002 1000ff 7ffffc 500003 200000 100002 500001 200000 100001 500003
  //   100001 600005 200000 100006 500003 7ffffd 5ffffd 600015 600008 5fffff 100008 5fffff 100002 500002
  //   1000ff 7ffffa 100001 5fffff 800001 5fffff 600006 500001 1000fc 5fffff 1000ff 7ffffc 5fffff 7fffed
  //   5ffffe 600028 500005 600023 500003 200000 100009 5fffff 600006 500001 1000ff 5fffff 1000ff 7ffffc
  //   100009 500001 60000d 1000ff 600006 5fffff 1000ff 500001 1000ff 7ffffc 100001 600003 5ffffd 7fffff
  //   7ffff5 5fffff 600006 500001 100001 5fffff 1000ff 7ffffc 500001 7fffdf 5ffffe 1000ff 7fffda 5ffffe
  //   1000ff 7fffa1 900000
endmodule
